# Fritzing sketch Wiring (saved by Fritzing 0.9.2b)
breadboards: 1

parts:
  Raspberry_Pi1 = Raspberry Pi 2
  S1 = Pushbutton [package="[THT]"]
  R1 = Resistor [tolerance=±5% resistance=330 package=THT]
  R2 = Resistor [tolerance=±5% resistance=330 package=THT]
  LED1 = LED - 5mm [color="Red (633nm)" package="5 mm [THT]"]
  LED2 = LED - 5mm [color="Green (560nm)" package="5 mm [THT]"]

nets:
  N1: Raspberry_Pi1.GPIO17, S1.Pin_1, S1.Pin_2
  N2: Raspberry_Pi1.GND, S1.Pin_3, S1.Pin_4, R1.Pin_1, R2.Pin_1
  N3: Raspberry_Pi1.GPIO24, LED2.cathode
  N4: Raspberry_Pi1.GPIO23, LED1.cathode
  N5: R1.Pin_0, LED2.anode
  N6: R2.Pin_0, LED1.anode
